# Fritzing sketch Neopixel Window Candles (saved by Fritzing 0.9.9b)
circuit board: 2.36652cm x 3.14169cm
breadboards: 1

parts:
  R1 = Resistor [tolerance=±5% resistance=330 package=THT]
  Seeduino_Xiao = seeeduino-xiao
  R2 = Resistor [tolerance=±5% power=0.25 resistance=10k package=THT]
  R3 = Photocell (LDR) [package=THT]
  JP1 = Header 2 [package=jst-2-pth-ns]

nets:
  N1: R1.Pin_0, Seeduino_Xiao.D7
  N2: Seeduino_Xiao.D6, R2.Pin_1, R3.pin_0
  N3: Seeduino_Xiao.GND, R2.Pin_0, JP1.1
  N4: Seeduino_Xiao.5V, R3.pin_1, JP1.2

notes:
  Gnd
  Data
  3.3v
  330Ω
  Xiao
  Seeeduino
  USB
  Bottom
  10kΩ
  Photo

custom parts:
  seeeduino-xiao: Seeeduino XIAO processor board.
