# Fritzing sketch morseCodeTransmitter (saved by Fritzing 0.9.6b)
circuit board: 8.46667cm x 5.64444cm
breadboards: 1

parts:
  LED1 = LEDs [package=led10mm]
  Buzzer = Piezo Speaker
  S1 = Square Pushbutton
  R2 = Resistor [tolerance=±5% resistance=220 package="0603 [SMD]"]
  R1 = Resistor [tolerance=±5% resistance=220 package="0603 [SMD]"]
  Part1 = Arduino Nano Every
  Part2 = NRF24L01+ Breakout Board
  IC1 = Voltage Regulator [package=to220-igo]
  C1 = Capacitor [package=cap-pth-small2]
  BAT1 = BC9VPC [package=bc9vpc]
  C2 = Capacitor [package=cap-pth-small2]

nets:
  N1: LED1.C, R1.Pin_0
  N2: LED1.A, Part1.D10~
  N3: Buzzer.pin1, Part1.D3~
  N4: Buzzer.pin2, R2.Pin_1, R1.Pin_1, Part2.GND, IC1.IN, C1.2, BAT1.V-, C2.1
  N5: S1.leg0, R2.Pin_0, Part1.D2
  N6: S1.leg1, Part2.VCC, IC1.OUT, C1.1
  N7: Part1.RESET, Part1.A7
  N8: Part1.GND, Part1.D13~
  N9: Part1.D7, Part2.CE
  N10: Part1.D8, Part2.CS
  N11: Part1.D11/MOSI, Part1.+5V
  N12: IC1.GND, BAT1.V+, C2.2

custom parts:
  Arduino Nano Every: The Nano Every is Arduino’s 5V compatible board in the smallest available form factor: 45x18mm! The Arduino Nano is the preferred board for many projects requiring a small and easy to use microcontroller board. The small footprint and low price, make the Nano Every particularly suited for wearable inventions, low cost robotics, electronic musical instruments, and general use to control smaller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
